# Fritzing sketch breadboard-nodemcu-wind-power-monitor-mcp3208 (saved by Fritzing 0.9.3b)
breadboards: 5

parts:
  U1 = NodeMCU V1.0
  R1 = Resistor [tolerance=±5% resistance=22k package="0805 [SMD]"]
  U2 = Voltage Regulator - 3.3V [package="TO220 [THT]"]
  C1 = Capacitor Polarized [package=panasonic_c]
  S1 = SWITCH-MOMENTARY-2 [package=reed_switch_pth]
  J1 = Power Jack [package=power_jack_pth]
  R5 = Resistor [tolerance=±5% resistance=22k package="0805 [SMD]"]
  S2 = SWITCH-MOMENTARY-2 [package=reed_switch_pth]
  IC1 = MCP3208 8-channel 12-bit ADC [part_number=MCP3208]
  R6 = Resistor [tolerance=±5% resistance=1k package="0402 [SMD]"]
  Bauteil2 = ACS712 Low Current Sensor Board v12
  Bauteil3 = ACS712 Low Current Sensor Board v12
  Q2 = TRANSISTOR_NPN [package=to-92]
  R7 = Resistor [tolerance=±5% resistance=1k package="0402 [SMD]"]
  R8 = Resistor [tolerance=±5% resistance=100k package="0402 [SMD]"]
  R9 = Resistor [tolerance=±5% resistance=4.7k package="0402 [SMD]"]
  R10 = Resistor [tolerance=±5% resistance=4.7k package="0402 [SMD]"]
  R11 = Resistor [tolerance=±5% resistance=100k package="0402 [SMD]"]
  R12 = Temperature Sensor (Thermistor) [thermistor_type=NTC package=THT]
  R13 = Resistor [tolerance=±5% resistance=220 package="0603 [SMD]"]
  R14 = Resistor [tolerance=±5% resistance=10k package="0402 [SMD]"]
  Q3 = Basic FET N-Channel [package="D2Pak [SMD]"]
  LED1 = LED - 5mm [color="Red (633nm)" package="5 mm [THT]"]
  U3 = Optocoupler [package=THT]  # not connected

nets:
  N1: U1.D1, R5.Pin_0
  N2: U1.D2, R1.Pin_1
  N3: U1.D3, R6.Pin_1
  N4: U1.D4, R7.Pin_1
  5V: U1.3V3, R1.Pin_0, U2.output_voltage, C1.+, S1.1, R5.Pin_1, S2.2, IC1.15, IC1.16, Bauteil2.5V, Bauteil3.5V, R12.pin_0
  GND: U1.GND, U2.GND, C1.-, S1.2, J1.GND, S2.1, IC1.9, IC1.14, R13.Pin_0
  N5: U1.D5, IC1.10
  N6: U1.D6, IC1.11
  N7: U1.D7, IC1.12
  N8: U1.D8, IC1.13
  N9: U2.input_voltage, J1.PWR, R14.Pin_0
  N10: IC1.1, Bauteil2.VO
  N11: IC1.2, Bauteil3.VO
  N12: IC1.3, R8.Pin_1, R9.Pin_0
  N13: IC1.4, R10.Pin_0, R11.Pin_1
  N14: IC1.5, R12.pin_1, R13.Pin_1
  N15: R6.Pin_0, Q2.B
  GND_2: Bauteil2.GND, Bauteil3.GND, R9.Pin_1, R10.Pin_1
  N16: Q2.E, R14.Pin_1, Q3.Gate
  N17: Q2.C, Q3.source
  N18: Q3.drain, LED1.cathode

notes:
  reed switches in anemometer and rpm-meter
  12V lead acid battery
  3.3V stable power supply for nodemcu
  8x 12Bit AD channels
  SD-Card
  Adapter
  12+V mosfet
  to switch
  dump load
  ACS power measuring
  voltage divider for measuring battery charge state
  battery
  thermometer
  resistor not too high for fast switchings
  opto koppler
  mosfet driver
  eg ir4426/ir4427

custom parts:
  NodeMCU V1.0: ESP8266 based NodeMCU
  MCP3208 8-channel 12-bit ADC: 12-bit resolution ± 1 LSB max DNL ± 1 LSB max INL (MCP3204/3208-B) ± 2 LSB max INL (MCP3204/3208-C) 4 (MCP3204) or 8 (MCP3208) input channels Analog inputs programmable as single-ended or pseudo differential pairs On-chip sample and hold SPI ® serial interface (modes 0,0 and 1,1) Single supply operation: 2.7V - 5.5V 100ksps max. sampling rate at V DD = 5V 50ksps max. sampling rate at V DD =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
