# Fritzing sketch pcb-nodemcu_mcp3208 (saved by Fritzing 0.9.3b)
circuit board: 8.1cm x 5.1cm
breadboards: 1

parts:
  U1 = NodeMCU V1.0
  R1 = Resistor [tolerance=±5% resistance=220 package=THT]
  R2 = Resistor [tolerance=±5% resistance=220 package=THT]
  R4 = Resistor [tolerance=±5% resistance=220 package=THT]
  R5 = Resistor [tolerance=±5% resistance=220 package=THT]
  R6 = Resistor [tolerance=±5% resistance=220 package=THT]
  R8 = Resistor [tolerance=±5% resistance=220 package=THT]
  R7 = Resistor [tolerance=±5% resistance=220 package=THT]
  R10 = Resistor [tolerance=±5% resistance=220 package=THT]
  R9 = Resistor [tolerance=±5% resistance=220 package=THT]
  JP14 = Header 12 [package=1x12_machine-pin-header_lock.004]
  J3 = Camdenboss CTB0158-2 [part_number=CTB0158-2 package=THT]
  JP15 = Header 1 [package=1x01_offset]
  JP16 = Header 1 [package=1x01_offset]
  JP17 = Header 1 [package=1x01_offset]
  J2 = Camdenboss CTB0158-10 [part_number=CTB0158-10 package=THT]
  J4 = Camdenboss CTB0158-2 [part_number=CTB0158-2 package=THT]
  J5 = Camdenboss CTB0158-8 [part_number=CTB0158-8 package=THT]
  JP21 = Header 12 [package=1x12_machine-pin-header_lock.004]
  JP22 = Header 12 [package=1x12_machine-pin-header_lock.004]
  JP23 = Header 3 [package=molex-1x3_lock]  # not connected
  JP24 = Header 3 [package=molex-1x3_lock]
  R18 = Resistor [tolerance=±5% resistance=0 package=THT]
  D1 = Zener Diode [part_number=1N4732A breakdown_voltage=3.6V package="300 mil [THT]"]
  D2 = Zener Diode [part_number=1N4732A breakdown_voltage=3.6V package="300 mil [THT]"]
  D3 = Zener Diode [part_number=1N4732A breakdown_voltage=3.6V package="300 mil [THT]"]
  R3 = Resistor [tolerance=±5% resistance=220 package=THT]
  IC1 = MCP3208 8-channel 12-bit ADC [part_number=MCP3208]

nets:
  N1: U1.D2, J5.pin3
  N2: U1.D3, R10.Pin_0
  N3: U1.D4, R9.Pin_0
  N4: U1.3V3, JP14.3, J4.pin1
  N5: U1.GND, R1.Pin_1, R5.Pin_1, R8.Pin_0, R7.Pin_0, JP14.4, J3.pin2, J2.pin6, J2.pin8, J2.pin10, J4.pin2, J5.pin2, J5.pin4, J5.pin6, J5.pin8, JP21.2, JP22.2, D2.anode, D3.anode, R3.Pin_1, IC1.11
  N6: U1.Vin, J3.pin1
  N7: U1.RST, JP14.1
  N8: U1.EN, JP14.2
  N9: U1.CLK, JP14.5
  N10: U1.SD0, JP14.6
  N11: U1.CMD, JP14.7
  N12: U1.SD1, JP14.8
  N13: U1.SD2, JP14.9
  N14: U1.SD3, JP14.10
  N15: U1.RSV#40, JP14.11
  N16: U1.RSV#41, JP14.12
  N17: R1.Pin_0, R2.Pin_0, D1.cathode, IC1.8
  N18: R2.Pin_1, J2.pin9
  N19: R4.Pin_0, D2.cathode, R3.Pin_0, IC1.7
  N20: R4.Pin_1, J2.pin7
  N21: R5.Pin_0, R6.Pin_0, D3.cathode, IC1.6
  N22: R6.Pin_1, J2.pin5
  N23: R8.Pin_1, J2.pin3, IC1.1
  N24: R7.Pin_1, J2.pin4, IC1.2
  N25: R10.Pin_1, J5.pin5
  N26: R9.Pin_1, J5.pin7
  N27: JP15.1, IC1.5
  N28: JP16.1, IC1.4
  N29: JP17.1, IC1.3
  N30: J2.pin1, J2.pin2, R18.Pin_1
  N31: J5.pin1, JP24.2
  N32: JP22.5, IC1.12
  N33: JP22.6, IC1.13
  N34: JP22.7, IC1.14
  N35: JP22.8, IC1.15
  N36: JP22.9, IC1.16
  N37: JP22.10, R18.Pin_0
  N38: IC1.9, IC1.10

notes:
  Eddy-2-Power
  Charge Controller

custom parts:
  NodeMCU V1.0: ESP8266 based NodeMCU
  MCP3208 8-channel 12-bit ADC: 12-bit resolution ± 1 LSB max DNL ± 1 LSB max INL (MCP3204/3208-B) ± 2 LSB max INL (MCP3204/3208-C) 4 (MCP3204) or 8 (MCP3208) input channels Analog inputs programmable as single-ended or pseudo differential pairs On-chip sample and hold SPI ® serial interface (modes 0,0 and 1,1) Single supply operation: 2.7V - 5.5V 100ksps max. sampling rate at V DD = 5V 50ksps max. sampling rate at V DD =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
