# Fritzing sketch Entladeschutz (saved by Fritzing 0.9.3b)
breadboards: 1

parts:
  U1 = 555 Timer [package="SO8 [SMD]"]
  IC1 = Voltage Regulator [package=to-92]
  D1 = Diode [package=diode-hv]
  U3 = RELAY [package=OJ]
  R2 = Resistor [tolerance=±5% resistance=33k package=THT]
  R4 = Resistor [tolerance=±5% resistance=22k package=THT]
  C1 = Capacitor [package=cap-pth-small2]
  R5 = Resistor [tolerance=±5% resistance=15k package=THT]
  R6 = Resistor [tolerance=±5% resistance=10k package=THT]
  R7 = Rotary Potentiometer (Small) [maximum_resistance=10kΩ package=THT]
  R8 = Rotary Potentiometer (Small) [maximum_resistance=100kΩ package=THT]
  R10 = Resistor [tolerance=±5% resistance=10k package=THT]
  C2 = Electrolytic Capacitor [capacitance=100μF voltage=20V package="0807 [SMD, electrolytic]"]
  D3 = Diode [package=diode-1n4148]  # not connected

nets (from the breadboard view):
  N1: U1.Pin_1, IC1.GND, U3.COIL1, C1.1, R5.Pin_1, R6.Pin_1, C2.-
  N2: U1.Pin_2, R6.Pin_0, R8.wiper
  N3: U1.Pin_3, R10.Pin_0
  N4: U1.Pin_5, C1.2
  N5: U1.Pin_6, R5.Pin_0, R7.wiper
  N6: U1.Pin_8, IC1.OUT, D1.C, C2.+
  N7: IC1.IN, R2.Pin_0, R4.Pin_0
  N8: D1.A, U3.COIL2, R10.Pin_1
  N9: R2.Pin_1, R8.leg2
  N10: R4.Pin_1, R7.leg1
