# Fritzing sketch MCP3008_an_Pi_mit_Spannungsteiler (saved by Fritzing 0.9.3b)
breadboards: 1

parts:
  R1 = Resistor [tolerance=±5% resistance=10k package=THT]
  R2 = Resistor [tolerance=±5% resistance=2.2k package=THT]
  IC1 = MCP3008 8-channel 10-bit ADC [part_number=MCP3008]
  Raspberry_Pi_B_rev1 = Raspberry Pi B rev1
  Bauteil1 = ACS712 Low Current Sensor Board v12
  Z1 = DIODE-ZENER [part_number=3,3V package=diode-zener]
  R4 = Resistor [tolerance=±5% resistance=15k package="0805 [SMD]"]
  R3 = Resistor [tolerance=±5% resistance=33k package="0805 [SMD]"]
  Z2 = DIODE-ZENER [part_number=3,3V package=diode-zener]  # not connected

nets:
  N1: R1.Pin_1, R2.Pin_0, IC1.no_name_yet#1, Z1.C
  GND: R2.Pin_1, IC1.no_name_yet#9, IC1.no_name_yet#14, Raspberry_Pi_B_rev1.GND, Bauteil1.GND, R3.Pin_0
  N2: IC1.no_name_yet#8, R4.Pin_0, R3.Pin_1
  N3: IC1.no_name_yet#10, Raspberry_Pi_B_rev1.GPIO_8
  N4: IC1.no_name_yet#11, Raspberry_Pi_B_rev1.GPIO_10
  N5: IC1.no_name_yet#12, Raspberry_Pi_B_rev1.GPIO_9
  N6: IC1.no_name_yet#13, Raspberry_Pi_B_rev1.GPIO_11
  N7: IC1.no_name_yet#15, IC1.no_name_yet#16, Raspberry_Pi_B_rev1.3V3
  5V: Raspberry_Pi_B_rev1.5V, Bauteil1.5V
  N8: Bauteil1.VO, R4.Pin_1

notes:
  0 - 15V max.
  max. 30A
