# Fritzing sketch Spannungsteiler (saved by Fritzing 0.9.3b)
breadboards: 1

parts:
  U1 = atmega328 [package=dip]
  C1 = Ceramic Capacitor [capacitance=22pF package="100 mil [THT, multilayer]"]
  C2 = Ceramic Capacitor [capacitance=22pF package="100 mil [THT, multilayer]"]
  Quarz = Crystal [frequency="16 MHz" package=THT]
  R1 = Resistor [tolerance=±5% resistance=10k package=THT]
  R2 = Resistor [tolerance=±5% resistance=4.7k package=THT]
  R3 = Resistor [tolerance=±5% resistance=10k package=THT]
  Reset_Switch = Pushbutton [package="[THT]"]
  Z1_5_1V = DIODE-ZENER [package=diode-zener]  # not connected

nets:
  N1: U1.RESET, R3.Pin_0, Reset_Switch.Pin_1, Reset_Switch.Pin_2
  N2: U1.VCC, R3.Pin_1
  N3: U1.GND#7, C1.1, C2.1, Reset_Switch.Pin_3, Reset_Switch.Pin_4
  N4: U1.XLAT1, C2.0, Quarz.pin_0
  N5: U1.XLAT2, C1.0, Quarz.pin_1
  N6: U1.AVCC, U1.AREF
  N7: U1.A0, R1.Pin_1, R2.Pin_0
