# Fritzing sketch nodemcu-sdcard (saved by Fritzing 0.9.3b)

parts:
  U1 = NodeMCU V1.0
  SD_Card_Pins = Camdenboss CTB0158-8 [part_number=CTB0158-8 package=THT]

nets:
  N1: U1.3V3, SD_Card_Pins.terminal_5
  N2: U1.GND, SD_Card_Pins.terminal_4, SD_Card_Pins.terminal_7
  N3: U1.D5, SD_Card_Pins.terminal_6
  N4: U1.D6, SD_Card_Pins.terminal_8
  N5: U1.D7, SD_Card_Pins.terminal_3
  N6: U1.D8, SD_Card_Pins.terminal_2

notes:
  SD Card Pins
  9 1 2 3 4 5 6 7 8

custom parts:
  NodeMCU V1.0: ESP8266 based NodeMCU
