# Fritzing sketch arduino_reset_via_pi-gpio (saved by Fritzing 0.9.0b)

parts:
  Raspberry_Pi = Raspberry Pi B rev2
  Arduino = Arduino Uno (Rev3)

nets:
  N1: Raspberry_Pi.GPIO_3, Raspberry_Pi.GPIO_14, Raspberry_Pi.GPIO_4, Arduino.RESET
