# Fritzing sketch sensors_arduino_pi (saved by Fritzing 0.9.0b)
breadboards: 1

parts:
  S1_Anemometer_Reed_Switch = Reed switch [package=THT]
  Bauteil1 = Arduino Mega ADK (Rev3)
  Raspberry_Pi_B_rev1 = Raspberry Pi B rev2
  S2_Windrad_Reed_Switch = Reed switch [package=THT]

nets:
  N1: S1_Anemometer_Reed_Switch.pin_1, Raspberry_Pi_B_rev1.GPIO_23
  N2: Bauteil1.RESET, Raspberry_Pi_B_rev1.GPIO_4
  N3: Raspberry_Pi_B_rev1.GPIO_22, S2_Windrad_Reed_Switch.pin_1
