# Fritzing sketch nodemcu-wind-power-monitor-mcp3208-relays (saved by Fritzing 0.9.3b)
breadboards: 5

parts:
  U1 = NodeMCU V1.0
  R1 = Resistor [tolerance=±5% resistance=22k package="0805 [SMD]"]
  U2 = Voltage Regulator - 3.3V [package="TO220 [THT]"]
  C1 = Capacitor Polarized [package=panasonic_c]
  S1 = SWITCH-MOMENTARY-2 [package=reed_switch_pth]
  J1 = Power Jack [package=power_jack_pth]
  R5 = Resistor [tolerance=±5% resistance=22k package="0805 [SMD]"]
  S2 = SWITCH-MOMENTARY-2 [package=reed_switch_pth]
  IC1 = MCP3208 8-channel 12-bit ADC [part_number=MCP3208]
  Bauteil1 = MicroSD Card Module  # not connected
  U3 = RELAY [package=relay-t9a-2]
  Q1 = TRANSISTOR_NPN [package=to-92]
  R6 = Resistor [tolerance=±5% resistance=1k package="0402 [SMD]"]
  Bauteil2 = ACS712 Low Current Sensor Board v12
  Bauteil3 = ACS712 Low Current Sensor Board v12
  Q2 = TRANSISTOR_NPN [package=to-92]
  R7 = Resistor [tolerance=±5% resistance=1k package="0402 [SMD]"]
  U4 = RELAY [package=relay-t9a-2]
  R8 = Resistor [tolerance=±5% resistance=220 package="0402 [SMD]"]
  R9 = Resistor [tolerance=±5% resistance=220 package="0402 [SMD]"]
  R10 = Resistor [tolerance=±5% resistance=220 package="0402 [SMD]"]
  R11 = Resistor [tolerance=±5% resistance=220 package="0402 [SMD]"]
  D3 = Diode [package=diode-1n4148]
  D4 = Diode [package=diode-1n4148]
  R12 = Temperature Sensor (Thermistor) [thermistor_type=NTC package=THT]
  R13 = Resistor [tolerance=±5% resistance=220 package="0603 [SMD]"]

nets:
  N1: U1.D1, R5.Pin_0
  N2: U1.D2, R1.Pin_1
  N3: U1.D3, R6.Pin_1
  N4: U1.D4, R7.Pin_1
  N5: U1.3V3, R1.Pin_0, U2.output_voltage, C1.+, S1.1, R5.Pin_1, S2.2, IC1.15, IC1.16, R12.pin_0
  GND: U1.GND, U2.GND, C1.-, S1.2, J1.GND, S2.1, IC1.9, IC1.14, R13.Pin_0
  N6: U1.D5, IC1.10
  N7: U1.D6, IC1.11
  N8: U1.D7, IC1.12
  N9: U1.D8, IC1.13
  N10: U2.input_voltage, J1.PWR, U3.COIL1, D4.C
  N11: IC1.1, Bauteil2.VO
  N12: IC1.2, Bauteil3.VO
  N13: IC1.3, R8.Pin_1, R9.Pin_0
  N14: IC1.4, R10.Pin_0, R11.Pin_1
  N15: IC1.5, R12.pin_1, R13.Pin_1
  N16: U3.COIL2, Q1.C, D4.A
  N17: U3.NO, R11.Pin_0
  N18: Q1.E, Q2.E, U4.COIL1, D3.C
  N19: Q1.B, R6.Pin_0
  5V: Bauteil2.5V, Bauteil3.5V
  GND_2: Bauteil2.GND, Bauteil3.GND, R9.Pin_1, R10.Pin_1
  N20: Q2.B, R7.Pin_0
  N21: Q2.C, U4.COIL2, D3.A
  N22: U4.NO, R8.Pin_0

notes:
  reed switches in anemometer and rpm-meter
  12V lead acid battery
  3.3V stable power supply for nodemcu
  8x 12Bit AD channels
  SD-Card
  Adapter
  12V relay to switch
  dump load
  12V relay to switch second dump load
  ACS power measuring
  voltage divider for measuring battery charge state
  battery
  thermometer

custom parts:
  NodeMCU V1.0: ESP8266 based NodeMCU
  MCP3208 8-channel 12-bit ADC: 12-bit resolution ± 1 LSB max DNL ± 1 LSB max INL (MCP3204/3208-B) ± 2 LSB max INL (MCP3204/3208-C) 4 (MCP3204) or 8 (MCP3208) input channels Analog inputs programmable as single-ended or pseudo differential pairs On-chip sample and hold SPI ® serial interface (modes 0,0 and 1,1) Single supply operation: 2.7V - 5.5V 100ksps max. sampling rate at V DD = 5V 50ksps max. sampling rate at V DD =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
