# Fritzing sketch nodemcu-wind-power-monitor-mcp3208 (saved by Fritzing 0.9.3b)
breadboards: 1

parts:
  U1 = NodeMCU V1.0
  R1 = Resistor [tolerance=±5% resistance=22k package="0805 [SMD]"]
  R3 = Resistor [tolerance=±5% resistance=22k package="0805 [SMD]"]
  R4 = Resistor [tolerance=±5% resistance=330k package="0805 [SMD]"]
  U2 = Voltage Regulator - 3.3V [package="TO220 [THT]"]
  C1 = Capacitor Polarized [package=panasonic_c]
  S1 = SWITCH-MOMENTARY-2 [package=reed_switch_pth]
  J1 = Power Jack [package=power_jack_pth]
  R5 = Resistor [tolerance=±5% resistance=22k package="0805 [SMD]"]
  S2 = SWITCH-MOMENTARY-2 [package=reed_switch_pth]
  Bauteil1 = MicroSD Card Module
  IC1 = MCP3208 8-channel 12-bit ADC [part_number=MCP3208]

nets:
  N1: U1.D1, R5.Pin_0
  N2: U1.D2, R1.Pin_1
  3V3: U1.3V3, R1.Pin_0, U2.output_voltage, C1.+, S1.1, R5.Pin_1, S2.2, Bauteil1.VCC, IC1.15, IC1.16
  GND: U1.GND, R3.Pin_0, U2.GND, C1.-, S1.2, J1.GND, S2.1, Bauteil1.GND, IC1.9, IC1.14
  N3: U1.CLK, Bauteil1.SCK, IC1.13
  N4: U1.SD0, Bauteil1.MISO, IC1.11
  N5: U1.CMD, Bauteil1.CS
  N6: U1.SD1, Bauteil1.MOSI, IC1.12
  N7: U1.SD2, IC1.10
  N8: U1.A0, R3.Pin_1, R4.Pin_0
  N9: R4.Pin_1, U2.input_voltage, J1.PWR

notes:
  reed switches in anemometer and rpm-meter
  12V lead acid battery
  3.3V stable power supply for nodemcu
  8x 12Bit AD channels

custom parts:
  NodeMCU V1.0: ESP8266 based NodeMCU
  MCP3208 8-channel 12-bit ADC: 12-bit resolution ± 1 LSB max DNL ± 1 LSB max INL (MCP3204/3208-B) ± 2 LSB max INL (MCP3204/3208-C) 4 (MCP3204) or 8 (MCP3208) input channels Analog inputs programmable as single-ended or pseudo differential pairs On-chip sample and hold SPI ® serial interface (modes 0,0 and 1,1) Single supply operation: 2.7V - 5.5V 100ksps max. sampling rate at V DD = 5V 50ksps max. sampling rate at V DD =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
