# Fritzing sketch nodemcu-wind-power-monitor (saved by Fritzing 0.9.3b)
breadboards: 1

parts:
  U1 = NodeMCU V1.0
  R1 = Resistor [tolerance=±5% resistance=22k package="0805 [SMD]"]
  R3 = Resistor [tolerance=±5% resistance=22k package="0805 [SMD]"]
  R4 = Resistor [tolerance=±5% resistance=330k package="0805 [SMD]"]
  U2 = Voltage Regulator - 3.3V [package="TO220 [THT]"]
  C1 = Capacitor Polarized [package=panasonic_c]
  S1 = SWITCH-MOMENTARY-2 [package=reed_switch_pth]
  J1 = Power Jack [package=power_jack_pth]
  R5 = Resistor [tolerance=±5% resistance=22k package="0805 [SMD]"]
  S2 = SWITCH-MOMENTARY-2 [package=reed_switch_pth]
  Bauteil1 = MicroSD Card Module
  IC1 = MCP3008 8-channel 10-bit ADC [part_number=MCP3008]  # not connected

nets:
  N1: U1.D1, R5.Pin_1, S2.2
  N2: U1.D2, R1.Pin_1, S1.2
  3V3: U1.3V3, R1.Pin_0, U2.output_voltage, C1.+, R5.Pin_0, Bauteil1.VCC
  GND: U1.GND, R3.Pin_0, U2.GND, C1.-, S1.1, J1.GND, S2.1, Bauteil1.GND
  N3: U1.CLK, Bauteil1.SCK
  N4: U1.SD0, Bauteil1.MISO
  N5: U1.CMD, Bauteil1.CS
  N6: U1.SD1, Bauteil1.MOSI
  N7: U1.A0, R3.Pin_1, R4.Pin_0
  N8: R4.Pin_1, U2.input_voltage, J1.PWR

notes:
  reed switches in anemometer and rpm-meter
  12V lead acid battery
  3.3V stable power supply for nodemcu

custom parts:
  NodeMCU V1.0: ESP8266 based NodeMCU
